// Logisim project NumberComparator.circ as structural Verilog: 1 circuit, main circuit main
module main (
  input  a4,
  input  b4,
  input  a3,
  input  b3,
  input  a2,
  input  b2,
  input  a1,
  input  b1,
  input  a0,
  input  b0
);

  wire and_1_out, and_2_out, and_3_out, and_4_out, and_5_out, and_6_out, and_7_out, and_8_out, nor_1_out,
       nor_2_out, nor_3_out, not_1_out, not_2_out, not_3_out, not_4_out, not_5_out, not_6_out, or_1_out,
       or_2_out, or_3_out, xnor_1_out, xnor_2_out, xnor_3_out, xnor_4_out, xnor_5_out;

  xnor xnor_1 (xnor_1_out, a4, b4);
  xnor xnor_2 (xnor_2_out, a3, b3);
  xnor xnor_3 (xnor_3_out, a2, b2);
  xnor xnor_4 (xnor_4_out, a1, b1);
  xnor xnor_5 (xnor_5_out, a0, b0);
  not not_1 (not_1_out, b4);
  not not_2 (not_2_out, b3);
  not not_3 (not_3_out, b2);
  not not_4 (not_4_out, b1);
  not not_5 (not_5_out, b0);
  and and_1 (and_1_out, a4, not_1_out);
  and and_2 (and_2_out, not_2_out, xnor_1_out, a3);
  and and_3 (and_3_out, xnor_2_out, xnor_1_out, not_3_out, a2);
  and and_4 (and_4_out, xnor_2_out, xnor_3_out, xnor_1_out, not_4_out, a1);
  and and_5 (and_5_out, xnor_1_out, xnor_2_out, xnor_3_out, not_5_out, a0);
  nor nor_1 (nor_1_out, a0, b0, a1, b1, a2, a3, b3, b4, a4);
  and and_6 (and_6_out, xnor_2_out, xnor_3_out, xnor_1_out, xnor_4_out, xnor_5_out);
  or or_1 (or_1_out, and_1_out, and_2_out, and_3_out, and_4_out, and_5_out);
  nor nor_2 (nor_2_out, and_6_out, or_1_out);
  not not_6 (not_6_out, nor_1_out);
  and and_7 (and_7_out, and_6_out, nor_1_out);
  and and_8 (and_8_out, not_6_out, not_6_out, and_6_out);
  or or_2 (or_2_out, and_8_out, nor_2_out);
  nor nor_3 (nor_3_out, nor_2_out, and_7_out);
  or or_3 (or_3_out, nor_3_out, and_8_out);

  // Notes on the sheet:
  //   a0: pull=up
  //   i3
  //   i2
  //   i1
  //   i0
  //   A = B = 0
  //   A > B
  //   A < B
  //   A = B != 0
  //   Q1
  //   Q0
endmodule
